// Logisim project ALU_32_BIT.circ as structural Verilog: 10 circuits, main circuit main
module main (
);

  ALU1Bit ALU ();  // open: A, B, Cin, ALU_Ctrl, R, Cout
endmodule

module Adder1Bit (
  input  A,
  input  B,
  input  Cin,
  output Sum,
  output Cout
);

  wire and_1_out, and_2_out, xor_1_out;

  xor xor_1 (xor_1_out, A, B);
  and and_1 (and_1_out, A, B);
  and and_2 (and_2_out, xor_1_out, Cin);
  xor xor_2 (Sum, xor_1_out, Cin);
  or or_1 (Cout, and_2_out, and_1_out);
endmodule

module Multi (
  input  A,
  input  B,
  input  Select1,
  input  Select0,
  output R
);

  wire and_1_out, and_2_out, and_3_out, and_4_out, not_1_out, not_2_out, not_3_out, not_4_out, or_1_out,
       or_2_out;

  and and_1 (and_1_out, A, B, not_1_out, not_2_out);
  not not_1 (not_1_out, Select1);
  not not_2 (not_2_out, Select0);
  and and_2 (and_2_out, A, B, not_3_out, Select0);
  not not_3 (not_3_out, Select1);
  and and_3 (and_3_out, A, B, Select1, not_4_out);
  not not_4 (not_4_out, Select0);
  and and_4 (and_4_out, A, B, Select1, Select0);
  or or_1 (or_1_out, and_1_out, and_2_out);
  or or_2 (or_2_out, and_3_out, and_4_out);
  or or_3 (R, or_1_out, or_2_out);
endmodule

module ALU1Bit (
  input  A,
  input  B,
  input  Cin,
  input  [3:0] ALU_Ctrl,
  output R,
  output Cout
);

  wire Adder_cout, Adder_sum, and_1_out, and_2_out, not_1_out, or_1_out, Subtracter_cout, Subtracter_sum,
       xor_1_out, xor_2_out;

  and and_1 (and_1_out, ALU_Ctrl[0], ALU_Ctrl[1], ALU_Ctrl[2], not_1_out);
  not not_1 (not_1_out, ALU_Ctrl[3]);
  xor xor_1 (xor_1_out, A, and_1_out);
  and and_2 (and_2_out, A, B);
  or or_1 (or_1_out, A, B);
  xor xor_2 (xor_2_out, A, B);
  Adder1Bit Adder (.A(A), .B(B), .Cin(Cin), .Sum(Adder_sum), .Cout(Adder_cout));
  Adder1Bit Subtracter (.A(B), .B(xor_1_out), .Cin(and_1_out), .Sum(Subtracter_sum), .Cout(Subtracter_cout));
  Multiplexer #(.enable("false"), .select(4)) multiplexer_1 (
    .in0(and_2_out), .in1(or_1_out), .in2(xor_2_out), .in3(Adder_sum), .in7(Subtracter_sum), .out(R),
    .sel(ALU_Ctrl));  // open: in4, in5, in6, in8, in9, in10, in11, in12, in13, in14, in15
  or or_2 (Cout, Adder_cout, Subtracter_cout);
endmodule

module ALU32Bit (
  input  [31:0] A,
  input  [31:0] B,
  input  [3:0] ALU_Ctrl,
  output [31:0] Result,
  output C_out
);

  wire ALU_0_3_cout, ALU_4_7_cout, ALU_8_11_cout, ALU_12_15_cout, ALU_16_19_cout, ALU_20_23_cout,
       ALU_24_27_cout;

  ALU4BIT ALU_0_3 (.A(A[3:0]), .B(B[3:0]), .ALU_CTRL(ALU_Ctrl), .R(Result[3:0]), .Cout(ALU_0_3_cout));  // open: Cin
  ALU4BIT ALU_4_7 (
    .A(A[7:4]), .B(B[7:4]), .Cin(ALU_0_3_cout), .ALU_CTRL(ALU_Ctrl), .R(Result[7:4]), .Cout(ALU_4_7_cout));
  ALU4BIT ALU_8_11 (
    .A(A[11:8]), .B(B[11:8]), .Cin(ALU_4_7_cout), .ALU_CTRL(ALU_Ctrl), .R(Result[11:8]), .Cout(ALU_8_11_cout));
  ALU4BIT ALU_12_15 (
    .A(A[15:12]), .B(B[15:12]), .Cin(ALU_8_11_cout), .ALU_CTRL(ALU_Ctrl), .R(Result[15:12]),
    .Cout(ALU_12_15_cout));
  ALU4BIT ALU_16_19 (
    .A(A[19:16]), .B(B[19:16]), .Cin(ALU_12_15_cout), .ALU_CTRL(ALU_Ctrl), .R(Result[19:16]),
    .Cout(ALU_16_19_cout));
  ALU4BIT ALU_20_23 (
    .A(A[23:20]), .B(B[23:20]), .Cin(ALU_16_19_cout), .R(Result[23:20]), .Cout(ALU_20_23_cout));  // open: ALU_CTRL
  ALU4BIT ALU_24_27 (
    .A(A[27:24]), .B(B[27:24]), .Cin(ALU_20_23_cout), .ALU_CTRL(ALU_Ctrl), .R(Result[27:24]),
    .Cout(ALU_24_27_cout));
  ALU4BIT ALU_28_31 (
    .A(A[31:28]), .B(B[31:28]), .Cin(ALU_24_27_cout), .ALU_CTRL(ALU_Ctrl), .R(Result[31:28]), .Cout(C_out));

  // Other names for the same wires on the sheet: A_0_3[3:0] = A[3:0]; A_4_7[3:0] = A[7:4]; A_8_11[3:0] = A[11:8];
  //   A_12_15[3:0] = A[15:12]; A_16_19[3:0] = A[19:16]; A_20_23[3:0] = A[23:20]; A_24_27[3:0] = A[27:24];
  //   A_28_31[3:0] = A[31:28]; B_0_3[3:0] = B[3:0]; B_4_7[3:0] = B[7:4]; B_8_11[3:0] = B[11:8];
  //   B_12_15[3:0] = B[15:12]; B_16_19[3:0] = B[19:16]; B_20_23[3:0] = B[23:20]; B_24_27[3:0] = B[27:24];
  //   B_28_31[3:0] = B[31:28]; C = C_out; CTRL[3:0] = ALU_Ctrl; R[31:0] = Result; R_0_3[3:0] = Result[3:0];
  //   R_4_7[3:0] = Result[7:4]; R_8_11[3:0] = Result[11:8]; R_12_15[3:0] = Result[15:12];
  //   R_16_19[3:0] = Result[19:16]; R_20_23[3:0] = Result[23:20]; R_24_27[3:0] = Result[27:24];
  //   R_28_31[3:0] = Result[31:28]
endmodule

module ALU4BIT (
  input  [3:0] A,
  input  [3:0] B,
  input  Cin,
  input  [3:0] ALU_CTRL,
  output [3:0] R,
  output Cout
);

  wire ALU0_cout, ALU1_cout, ALU2_cout;

  ALU1Bit ALU1 (.A(A[1]), .B(B[1]), .Cin(ALU0_cout), .ALU_Ctrl(ALU_CTRL), .R(R[1]), .Cout(ALU1_cout));
  ALU1Bit ALU0 (.A(A[0]), .B(B[0]), .Cin(Cin), .ALU_Ctrl(ALU_CTRL), .R(R[0]), .Cout(ALU0_cout));
  ALU1Bit ALU3 (.A(A[3]), .B(B[3]), .Cin(ALU2_cout), .ALU_Ctrl(ALU_CTRL), .R(R[3]), .Cout(Cout));
  ALU1Bit ALU2 (.A(A[2]), .B(B[2]), .Cin(ALU1_cout), .ALU_Ctrl(ALU_CTRL), .R(R[2]), .Cout(ALU2_cout));
endmodule

module ALU_Control (
  input  I30,
  input  I14,
  input  I13,
  input  I12,
  input  I6,
  input  I5,
  input  I4,
  output ALU_Ctrl3,
  output ALU_Ctrl2,
  output ALU_Ctrl1,
  output ALU_Ctrl0,
  output ALU_Src
);

  Ctrl1 ctrl1_1 (.I14(I14), .I13(I13), .I12(I12), .I6(I6), .I4(I4), .ALU_CTR1(ALU_Ctrl1));
  Ctrl0 ctrl0_1 (.I30(I30), .I14(I14), .I13(I13), .I12(I12), .I6(I6), .I5(I5), .I4(I4), .ALU_Ctrl0(ALU_Ctrl0));
  Src src_1 (.I14(I14), .I13(I13), .I12(I12), .I6(I6), .I5(I5), .I4(I4), .ALU_Src(ALU_Src));

  assign ALU_Ctrl2 = I30;
  assign ALU_Ctrl3 = 1'b0;
endmodule

module Ctrl0 (
  input  I30,
  input  I14,
  input  I13,
  input  I12,
  input  I6,
  input  I5,
  input  I4,
  output ALU_Ctrl0
);

  wire and_1_out, and_2_out, and_3_out, and_4_out;

  and and_1 (and_1_out, ~I14, ~I13, ~I12, ~I6, I4);  // AND_Gate
  and and_2 (and_2_out, ~I14, I13, ~I12, ~I6, ~I4);  // AND_Gate
  and and_3 (and_3_out, ~I30, I14, ~I13, ~I12, I4);  // AND_Gate
  and and_4 (and_4_out, I14, I13, ~I12, ~I6, ~I5, I4);  // AND_Gate
  or or_1 (ALU_Ctrl0, and_1_out, and_2_out, and_3_out, and_4_out);

  // Notes on the sheet:
  //   I14'I13'I12'I6'I4 
  //   I14'I1312'I6'I4'
  //   I30'I141312'I6'I4
  //   I14I13I12'I6'I5'I4
endmodule

module Ctrl1 (
  input  I14,
  input  I13,
  input  I12,
  input  I6,
  input  I4,
  output ALU_CTR1
);

  wire and_1_out, and_2_out;

  and and_1 (and_1_out, ~I13, ~I12, ~I12, I4);  // AND_Gate
  and and_2 (and_2_out, ~I14, I13, ~I12, ~I4);  // AND_Gate
  or or_1 (ALU_CTR1, and_1_out, and_2_out);

  // Notes on the sheet:
  //   I13' I12' I6' I4
  //   I14' I13 I12' I6' I4'
endmodule

module Src (
  input  I14,
  input  I13,
  input  I12,
  input  I6,
  input  I5,
  input  I4,
  output ALU_Src
);

  wire and_1_out, and_2_out, and_3_out;

  and and_1 (and_1_out, ~I13, ~I12, ~I6, ~I5, I4);  // AND_Gate
  and and_2 (and_2_out, ~I14, I13, ~I12, ~I6, ~I4);  // AND_Gate
  and and_3 (and_3_out, I14, I13, ~I6, ~I5, I4);  // AND_Gate
  or or_1 (ALU_Src, and_1_out, and_2_out, and_3_out);

  // Notes on the sheet:
  //   I13' I12' I6' I5' I4
  //   I14' I13 I12' I6' I4'
  //   I14 I13 I6' I5' I4
endmodule
